# Fritzing sketch home automation Sketch 2 (saved by Fritzing 0.9.3b)
breadboards: 1

parts:
  U1 = NodeMCU V1.0
  U2 = Module 4 Relais 5V [package="Module 4 Relais 5V"]
  Part1 = Breadboard Power Supply Board SMD
  S1 = SPST Switch [package=switch-spdt_lock.007s]
  S2 = SPST Switch [package=switch-spdt_lock.007s]
  S3 = SPST Switch [package=switch-spdt_lock.007s]
  S4 = SPST Switch [package=switch-spdt_lock.007s]
  LED1 = LED - 5mm [color="Red (633nm)" package="5 mm [THT]"]
  LED2 = LED - 5mm [color="Red (633nm)" package="5 mm [THT]"]
  LED3 = LED - 5mm [color="Red (633nm)" package="5 mm [THT]"]
  LED4 = LED - 5mm [color="Red (633nm)" package="5 mm [THT]"]

nets:
  N1: U1.D1, U2.IN3
  N2: U1.D3, U2.IN4
  GND: U1.GND, U2.GND, Part1.GND
  N3: U1.D5, U2.IN1
  N4: U1.D6, U2.IN2
  VCC: U1.Vin, U2.VCC, Part1.VCC
  N5: U2.K1-NF, LED4.cathode
  N6: U2.K2-NF, LED2.cathode
  N7: U2.K3-NF, LED3.cathode
  N8: U2.K4-NF, LED1.cathode
  N9: U2.K1-Com, S4.S
  N10: U2.K2-Com, S3.S
  N11: U2.K3-Com, S2.S
  N12: U2.K4-Com, S1.S
  N13: U2.K1-NO, S4.O
  N14: U2.K2-NO, S3.O
  N15: U2.K3-NO, S2.O
  N16: U2.K4-NO, S1.O

notes:
  NEUTRAL
  LIVE
  POWER ADAPTER 6-12V
  SINRIC
  ALEXA ANDROID APP
  AMAZON ECHO DOT
  INTERNET

custom parts:
  NodeMCU V1.0: ESP8266 based NodeMCU
  Module 4 Relais 5V: Module 4 Relais 5V 4x SPD-06VDC-SD-C
